# Fritzing sketch wiring (saved by Fritzing 0.9.2b)

parts:
  Part1 = Arduino Uno (Rev3)
  Part2 = Triple Axis Magnetometer - HMC5883 Breakout
  S1 = Pushbutton [package=THT]

nets:
  N1: Part1.A4/SDA, Part2.SDA
  N2: Part1.A5/SCL, Part2.SCL
  GND: Part1.GND, Part2.GND, S1.leg1
  N3: Part1.D2, S1.leg0
  5V: Part1.5V, Part2.VCC
